# Fritzing sketch esp32 (saved by Fritzing 0.9.3b)

parts:
  U1 = ESP32-38PinWide [part_number=ESP32-38PinWide]
  M1 = BME680 Module [part_number=CJMCU-680]
  A1 = MLX90640 camera module

nets:
  N1: U1.3.3, M1.VCC, A1.Pin_1
  GND: U1.GND, M1.GND, A1.Pin_2
  N2: U1.GPIO21, M1.SDA, A1.Pin_7
  N3: U1.GPIO22, M1.SCL, A1.Pin_8

custom parts:
  ESP32-38PinWide: Generic 38-Pin ESP32 with wide format (only access to one side of pins on a breadboard) based on Stephen Lilley's HiLetgo ESP-WROOM-32 ESP32 ESP-32S Development Board.
  BME680 Module: Bosch BME680 Development Module The BME680 is a digital 4-in-1 sensor that measures air quality [gas], humidity, pressure and temperature. Links: BME680 product datasheet
  MLX90640 camera module: MLX90640 camera module.
